// Logisim project half_adder.circ as structural Verilog
module main (
  input  in_1,
  input  b,
  input  s,
  input  c
);

  wire and_1_out, and_2_out, and_3_out, not_1_out, not_2_out, or_1_out;

  not not_1 (not_1_out, in_1);
  not not_2 (not_2_out, b);
  and and_1 (and_1_out, b, not_1_out);
  and and_2 (and_2_out, not_2_out, in_1);
  and and_3 (and_3_out, b, in_1);
  or or_1 (or_1_out, and_1_out, and_2_out);
endmodule
